// Logisim project t1.circ as structural Verilog
module somador_1bit (
  input  Ai,
  input  Bi,
  input  Ci,
  output Si,
  output Co
);

  wire and_1_out, and_2_out, and_3_out;

  xor xor_1 (Si, Ai, Bi, Ci);
  and and_1 (and_1_out, Ai, Bi);
  and and_2 (and_2_out, Ai, Ci);
  and and_3 (and_3_out, Bi, Ci);
  or or_1 (Co, and_1_out, and_2_out, and_3_out);
endmodule

module somador_8bit (
  input  [7:0] A,
  input  [7:0] B,
  input  C,
  output [7:0] out_4,
  output [7:0] out_5,
  output Co,
  output [7:0] out_7
);

  wire somador_1bit_1_co, somador_1bit_2_co, somador_1bit_3_co, somador_1bit_4_co, somador_1bit_5_co,
       somador_1bit_6_co, somador_1bit_7_co;

  somador_1bit somador_1bit_1 (.Ai(A[0]), .Bi(B[0]), .Ci(C), .Si(out_5[0]), .Co(somador_1bit_1_co));
  somador_1bit somador_1bit_2 (.Ai(A[1]), .Bi(B[1]), .Ci(somador_1bit_1_co), .Si(out_5[1]), .Co(somador_1bit_2_co));
  somador_1bit somador_1bit_3 (.Ai(A[2]), .Bi(B[2]), .Ci(somador_1bit_2_co), .Si(out_5[2]), .Co(somador_1bit_3_co));
  somador_1bit somador_1bit_4 (.Ai(A[3]), .Bi(B[3]), .Ci(somador_1bit_3_co), .Si(out_5[3]), .Co(somador_1bit_4_co));
  somador_1bit somador_1bit_5 (.Ai(A[4]), .Bi(B[4]), .Ci(somador_1bit_4_co), .Si(out_5[4]), .Co(somador_1bit_5_co));
  somador_1bit somador_1bit_6 (.Ai(A[5]), .Bi(B[5]), .Ci(somador_1bit_5_co), .Si(out_5[5]), .Co(somador_1bit_6_co));
  somador_1bit somador_1bit_7 (.Ai(A[6]), .Bi(B[6]), .Ci(somador_1bit_6_co), .Si(out_5[6]), .Co(somador_1bit_7_co));
  somador_1bit somador_1bit_8 (.Ai(A[7]), .Bi(B[7]), .Ci(somador_1bit_7_co), .Si(out_5[7]), .Co(Co));

  assign out_4 = A;
  assign out_7 = B;

  // Other names for the same wires on the sheet: S0 = out_5[0]; S1 = out_5[1]; S2 = out_5[2]; S3 = out_5[3];
  //   S4 = out_5[4]; S5 = out_5[5]; S6 = out_5[6]; S7 = out_5[7]

  // Notes on the sheet:
  //   Apagar
endmodule
