// Logisim project t2.circ as structural Verilog: 4 circuits, main circuit main
module main (
  input  [15:0] in_1,
  input  _1011_0110_10_010,
  input  [3:0] G,
  output [3:0] out_4,
  output [3:0] out_5,
  output [3:0] out_6,
  output [3:0] out_7
);

  wire button_1_out, multiplexer_1_out;
  wire [3:0] xor_1_out;

  Button button_1 (.out(button_1_out));
  cnt cnt_1 (.clk(button_1_out), .out_3(out_4));  // open: R
  Multiplexer #(.select(4), .enable("false")) multiplexer_1 (
    .in0(in_1[0]), .in1(in_1[1]), .in2(in_1[2]), .in3(in_1[3]), .in4(in_1[4]), .in5(in_1[5]), .in6(in_1[6]),
    .in7(in_1[7]), .in8(in_1[8]), .in9(in_1[9]), .in10(in_1[10]), .in11(in_1[11]), .in12(in_1[12]),
    .in13(in_1[13]), .in14(in_1[14]), .in15(in_1[15]), .out(multiplexer_1_out), .sel(out_4));
  Register #(.width(4)) register_1 (.D(out_5), .en(1'b1), .clk(button_1_out), .Q(out_7));  // open: clr
  assign xor_1_out = G ^ out_7;  // XOR_Gate xor_1, 4 bits wide
  Multiplexer #(.width(4), .enable("false")) multiplexer_2 (.in0(out_7), .in1(xor_1_out), .out(out_6), .sel(out_7[3]));
  bit_push_4bit bit_push_4bit_1 (.\bit (multiplexer_1_out), .v_in(out_6), .v_out(out_5));
endmodule

module bit_push (
  input  \bit ,
  input  [31:0] value,
  output [31:0] value_out
);


  assign value_out = {value[30:0], \bit };
endmodule

module bit_push_4bit (
  input  \bit ,
  input  [3:0] v_in,
  output [3:0] v_out
);


  assign v_out = {v_in[2:0], \bit };
endmodule

module cnt (
  input  clk,
  input  R,
  output [3:0] out_3
);

  wire t_ff_1_qn, t_ff_2_qn, t_ff_3_qn;

  T_Flip_Flop t_ff_1 (.T(1'b1), .clk(clk), .Q(out_3[0]), .Qn(t_ff_1_qn), .reset(R));  // open: preset
  T_Flip_Flop t_ff_2 (.T(1'b1), .clk(t_ff_1_qn), .Q(out_3[1]), .Qn(t_ff_2_qn), .reset(R));  // open: preset
  T_Flip_Flop t_ff_3 (.T(1'b1), .clk(t_ff_2_qn), .Q(out_3[2]), .Qn(t_ff_3_qn), .reset(R));  // open: preset
  T_Flip_Flop t_ff_4 (.T(1'b1), .clk(t_ff_3_qn), .Q(out_3[3]), .reset(R));  // open: Qn, preset
endmodule
